// Digital circuit DWAK2.dig as structural Verilog
module DWAK2 (
);

  ram ram_1 ();  // open: addr_read1, addr_read2, addr_write, data_write, store_write, clock, res_read1, res_read2
  instruction_memory instruction_memory_1 ();  // open: word_write, data_write, store_write, clock, word1, word2, word3, word4, word5, word6, word7, word8
  registers registers_1 ();  // open: reg_read1, reg_read2, reg_write, data_write, store_write, clock, res_read1, res_read2
endmodule
